# Fritzing sketch ELCO (saved by Fritzing 0.9.3b)
breadboards: 8

parts:
  WeMos_D1_Mini1 = WeMos D1 Mini
  DFRobot_DFPlayer_Mini1 = DFRobot DFPlayer Mini [part_number=DFR0299]
  SP1 = SPEAKER [package=pcb_mount_speaker]
  R1 = Resistor [tolerance=±5% resistance=1k package="0805 [SMD]"]
  R2 = Resistor [tolerance=±5% resistance=1k package="0805 [SMD]"]
  Componente1 = MPR121 Breakout
  Componente2 = MPR121 Breakout
  U1 = CAPSENSE_PAD [package=capsense_pad]
  S1 = Toggle Switch [package=THT]
  Componente3 = Power Cell LiPo Charger/Booster
  U3 = LIPO-1000mAh [package=lipo-1000]
  U4 = CAPSENSE_PAD [package=capsense_pad]
  U5 = CAPSENSE_PAD [package=capsense_pad]
  U6 = CAPSENSE_PAD [package=capsense_pad]
  U7 = CAPSENSE_PAD [package=capsense_pad]
  U8 = CAPSENSE_PAD [package=capsense_pad]
  U10 = CAPSENSE_PAD [package=capsense_pad]
  U11 = CAPSENSE_PAD [package=capsense_pad]
  U12 = CAPSENSE_PAD [package=capsense_pad]
  U13 = CAPSENSE_PAD [package=capsense_pad]
  U14 = CAPSENSE_PAD [package=capsense_pad]
  U15 = CAPSENSE_PAD [package=capsense_pad]
  U16 = CAPSENSE_PAD [package=capsense_pad]
  U17 = CAPSENSE_PAD [package=capsense_pad]
  U18 = CAPSENSE_PAD [package=capsense_pad]
  U19 = CAPSENSE_PAD [package=capsense_pad]
  U20 = CAPSENSE_PAD [package=capsense_pad]
  U21 = CAPSENSE_PAD [package=capsense_pad]
  U22 = CAPSENSE_PAD [package=capsense_pad]
  U23 = CAPSENSE_PAD [package=capsense_pad]
  Componente4 = ws2812b [package="smd 2812b"]
  Componente5 = ws2812b [package="smd 2812b"]
  Componente6 = ws2812b [package="smd 2812b"]
  Componente7 = ws2812b [package="smd 2812b"]
  Componente8 = ws2812b [package="smd 2812b"]
  Componente9 = ws2812b [package="smd 2812b"]
  Componente10 = ws2812b [package="smd 2812b"]
  Componente11 = ws2812b [package="smd 2812b"]
  Componente12 = ws2812b [package="smd 2812b"]
  Componente13 = ws2812b [package="smd 2812b"]
  Componente14 = ws2812b [package="smd 2812b"]
  Componente15 = ws2812b [package="smd 2812b"]
  Componente16 = ws2812b [package="smd 2812b"]
  Componente17 = ws2812b [package="smd 2812b"]
  Componente18 = ws2812b [package="smd 2812b"]
  Componente19 = ws2812b [package="smd 2812b"]
  Componente20 = ws2812b [package="smd 2812b"]
  Componente21 = ws2812b [package="smd 2812b"]
  Componente22 = ws2812b [package="smd 2812b"]
  R3 = Resistor [tolerance=±5% resistance=4.7k package="0805 [SMD]"]
  R4 = Resistor [tolerance=±5% resistance=4.7k package="0805 [SMD]"]
  R5 = Resistor [tolerance=±5% resistance=470 package="0805 [SMD]"]

nets:
  3.3V: WeMos_D1_Mini1.3V3, Componente1.3.3V, Componente2.3.3V
  VDD: WeMos_D1_Mini1.5V, DFRobot_DFPlayer_Mini1.VCC, S1.L2, Componente4.VDD, Componente5.VDD, Componente6.VDD, Componente7.VDD, Componente8.VDD, Componente9.VDD, Componente10.VDD, Componente11.VDD, Componente12.VDD, Componente13.VDD, Componente14.VDD, Componente15.VDD, Componente16.VDD, Componente17.VDD, Componente18.VDD, Componente19.VDD, Componente20.VDD, Componente21.VDD, Componente22.VDD, R3.Pin_1, R4.Pin_1
  N1: WeMos_D1_Mini1.D0, R5.Pin_0
  N2: WeMos_D1_Mini1.D1, Componente1.SCL
  N3: WeMos_D1_Mini1.D2, Componente1.ADDR, Componente1.SDA
  N4: WeMos_D1_Mini1.D3, R1.Pin_1
  N5: WeMos_D1_Mini1.D4, R2.Pin_1
  VSS: WeMos_D1_Mini1.G, DFRobot_DFPlayer_Mini1.GND-1, DFRobot_DFPlayer_Mini1.GND-2, Componente1.GND, Componente2.ADDR, Componente2.GND, U1.RECEIVE, Componente3.GND, Componente3.VBATT, U3.+, U3.-, U4.RECEIVE, U5.RECEIVE, U6.RECEIVE, U7.RECEIVE, U8.RECEIVE, U10.RECEIVE, U11.RECEIVE, U12.RECEIVE, U13.RECEIVE, U14.RECEIVE, U15.RECEIVE, U16.RECEIVE, U17.RECEIVE, U18.RECEIVE, U19.RECEIVE, U20.RECEIVE, U21.RECEIVE, U22.RECEIVE, U23.RECEIVE, Componente14.VSS, Componente15.VSS, Componente16.VSS, Componente17.VSS, Componente18.VSS, Componente19.VSS, Componente20.VSS, Componente21.VSS, Componente22.VSS
  N6: DFRobot_DFPlayer_Mini1.RX, R2.Pin_0
  N7: DFRobot_DFPlayer_Mini1.TX, R1.Pin_0
  N8: DFRobot_DFPlayer_Mini1.SPK_1, DFRobot_DFPlayer_Mini1.SPK_2, SP1.+, SP1.-
  N9: Componente1.ELE11, U1.RES
  N10: Componente1.ELE6, U4.RES
  N11: Componente1.ELE5, U5.RES
  N12: Componente1.ELE4, U6.RES
  N13: Componente1.ELE3, U7.RES
  N14: Componente1.ELE1, U10.RES
  N15: Componente1.ELE0, U11.RES
  N16: Componente2.SCL, R4.Pin_0
  N17: Componente2.ELE11, U12.RES
  N18: Componente2.ELE10, U13.RES
  N19: Componente2.ELE9, U14.RES
  N20: Componente2.ELE8, U15.RES
  N21: Componente2.ELE7, U16.RES
  N22: Componente2.ELE6, U17.RES
  N23: Componente2.ELE5, U18.RES
  N24: Componente2.ELE4, U19.RES
  N25: Componente2.ELE3, U20.RES
  N26: Componente2.ELE2, U21.RES
  N27: Componente2.ELE1, U22.RES
  N28: Componente2.ELE0, U23.RES
  N29: S1.COM, Componente3.5VIN
  N30: Componente4.DOUT, Componente5.DIN
  VSS_2: Componente4.VSS, Componente5.VSS, Componente6.VSS, Componente7.VSS, Componente8.VSS, Componente9.VSS, Componente10.VSS, Componente11.VSS, Componente12.VSS, Componente13.VSS
  N31: Componente4.DIN, R5.Pin_1
  N32: Componente5.DOUT, Componente6.DIN
  N33: Componente6.DOUT, Componente7.DIN
  N34: Componente7.DOUT, Componente8.DIN
  N35: Componente8.DOUT, Componente9.DIN
  N36: Componente9.DOUT, Componente10.DIN
  N37: Componente10.DOUT, Componente11.DIN
  N38: Componente11.DOUT, Componente12.DIN
  N39: Componente12.DOUT, Componente13.DIN
  N40: Componente13.DOUT, Componente14.DIN
  N41: Componente14.DOUT, Componente15.DIN
  N42: Componente15.DOUT, Componente16.DIN
  N43: Componente16.DOUT, Componente17.DIN
  N44: Componente17.DOUT, Componente18.DIN
  N45: Componente18.DOUT, Componente19.DIN
  N46: Componente19.DOUT, Componente20.DIN
  N47: Componente20.DOUT, Componente21.DIN
  N48: Componente21.DOUT, Componente22.DIN
